# Fritzing sketch Thermometer (saved by Fritzing 0.9.3b)
breadboards: 1

parts:
  RHT2 = Humidity and Temperature Sensor RHT03 [part_number=DHT22]
  U1 = NodeMCU V3.0

nets:
  VCC: RHT2.Vcc, U1.3V3
  N1: RHT2.Data-signal, U1.D1
  N2: RHT2.GND_2, U1.GND#6, U1.GND#13, U1.GND#16, U1.GND#33

custom parts:
  NodeMCU V3.0: ESP8266 based NodeMCU
